# Fritzing sketch schematics (saved by Fritzing 0.9.3b)

parts:
  NTD4806N-35G = MOSFET-NCHANNEL [package=to220v]
  Digispark_ATtiny85 = Digispark
  part = Resistor [tolerance=±5% resistance=1k package=THT]
  Touch_Sensor = TTP223B Capacitive Touch Sensor Module
  +12V = Power plug

nets:
  N1: NTD4806N-35G.G, part.Pin_1
  GND: NTD4806N-35G.S, Digispark_ATtiny85.GND, Touch_Sensor.GND, +12V.GND
  VCC: Digispark_ATtiny85.VCC, Touch_Sensor.VCC
  VIN: Digispark_ATtiny85.VIN, +12V.VCC
  N2: Digispark_ATtiny85.P2, Touch_Sensor.SIG
  N3: Digispark_ATtiny85.P4, part.Pin_0

custom parts:
  Digispark: The Digispark is an Attiny85 based microcontroller development board similar to the Arduino line, only cheaper, smaller, and a bit less powerful. With a whole host of shields to extend its functionality and the ability to use the familiar Arduino IDE the Digispark is a great way to jump into electronics, or perfect for when an Arduino is too big or too much.
  TTP223B Capacitive Touch Sensor Module: The TTP223B capacitive touch sensor module uses the TTP223B IC. The appropriate voltage is approximately 2 to 5.5 volts.
